# Fritzing sketch doorlock (saved by Fritzing 0.9.5d)
breadboards: 1

parts:
  Keypad4x1 = Keypad Membran 4x4
  Part1 = Arduino Uno (Rev3)
  J1 = Piezo Speaker
  LED1 = LED - 3mm [color="Green (555nm)" package="3 mm [THT]"]
  LED2 = LED - 3mm [color="Red (633nm)" package="3 mm [THT]"]
  R1 = Resistor [tolerance=±5% resistance=220 package="1206 [SMD]"]
  R2 = Resistor [tolerance=±5% resistance=220 package="1206 [SMD]"]
  M1 = Dagu DGServo 9g (End View) [part_number=RS001B]

nets:
  N1: Keypad4x1.Pin1, Part1.D9_PWM
  N2: Keypad4x1.Pin2, Part1.D8
  N3: Keypad4x1.Pin3, Part1.D7
  N4: Keypad4x1.Pin4, Part1.D6_PWM
  N5: Keypad4x1.Pin5, Part1.D5_PWM
  N6: Keypad4x1.Pin6, Part1.D4
  N7: Keypad4x1.Pin7, Part1.D3_PWM
  N8: Keypad4x1.Pin8, Part1.D2
  N9: Part1.D10_PWM/SS, M1.pulse
  N10: Part1.D11_PWM/MOSI, LED2.anode
  N11: Part1.D12/MISO, LED1.anode
  N12: Part1.D13/SCK, J1.pin2
  N13: Part1.GND, J1.pin1, R1.Pin_1, R2.Pin_1
  N14: LED1.cathode, R2.Pin_0
  N15: LED2.cathode, R1.Pin_0

custom parts:
  Keypad Membran 4x4: Membrane Keypad 4x4 Matrix
