# Fritzing sketch humidandtemplcd (saved by Fritzing 0.9.5d)
breadboards: 1

parts:
  LCD1 = LCD screen
  Part1 = Arduino Uno (Rev3)
  Mod1 = KY-015 Temperature & Humidity Sensor Module [package="Breakout board"]
  R1 = Trimmer Potentiometer [maximum_resistance=10kΩ package=THT]
  U1 = 74HC595 [package="DIP16 [THT]"]

nets:
  GND: LCD1.VSS, LCD1.LED-, Part1.GND, Mod1.Vin, Mod1.-, R1.leg2, U1.GND, U1.OE
  VDD: LCD1.VDD, LCD1.R/W, LCD1.LED+, Part1.5V, R1.leg1, U1.MR, U1.VCC
  N1: LCD1.V0, R1.wiper
  N2: LCD1.RS, U1.Q1
  N3: LCD1.E, U1.Q3
  N4: LCD1.DB4, U1.Q4
  N5: LCD1.DB5, U1.Q5
  N6: LCD1.DB6, U1.Q6
  N7: LCD1.DB7, U1.Q7
  N8: Part1.D9_PWM, U1.ST_CP
  N9: Part1.D11_PWM/MOSI, U1.DS
  N10: Part1.D13/SCK, U1.SH_CP
  N11: Part1.D4, Mod1.S

custom parts:
  KY-015 Temperature & Humidity Sensor Module: KY-015 temperature and humidity sensor module, provides a low-latency serial interface to measure humidity and temperature.
